// Logisim project zycClock.circ as structural Verilog: 1 circuit, main circuit main
module main (
);

  wire clock_1_out, n74160_1_p5, n74160_1_p7, n74160_3_p5, n74160_3_p7, n74160_5_p5, n74160_5_p7;
  wire [3:0] n74160_1_p10, n74160_2_p10, n74160_3_p10, n74160_4_p10, n74160_5_p10, n74160_6_p10;

  Hex_Digit_Display hex_digit_display_1 (.value(n74160_5_p10));  // open: dp
  Hex_Digit_Display hex_digit_display_2 (.value(n74160_6_p10));  // open: dp
  Clock #(.highDuration(1), .lowDuration(1)) clock_1 (.out(clock_1_out));
  Hex_Digit_Display hex_digit_display_3 (.value(n74160_3_p10));  // open: dp
  Hex_Digit_Display hex_digit_display_4 (.value(n74160_4_p10));  // open: dp
  Hex_Digit_Display hex_digit_display_5 (.value(n74160_1_p10));  // open: dp
  // _74160 74160_1: pin names not known; wires that end beside it: 1'b0, 1'b0, 1'b0, 1'b0, n74160_1_p5, n74160_1_p5, n74160_1_p7, 1'b1, clock_1_out, n74160_1_p10[0], n74160_1_p10[1], n74160_1_p10[2], n74160_1_p10[3]
  Hex_Digit_Display hex_digit_display_6 (.value(n74160_1_p10));  // open: dp
  Hex_Digit_Display hex_digit_display_7 (.value(n74160_2_p10));  // open: dp
  // _74160 74160_2: pin names not known; wires that end beside it: 1'b0, 1'b0, 1'b0, 1'b0, 1'b1, 1'b1, n74160_1_p7, 1'b1, clock_1_out, n74160_2_p10[0], n74160_2_p10[1], n74160_2_p10[2], n74160_2_p10[3], n74160_1_p5
  Hex_Digit_Display hex_digit_display_8 (.value(n74160_2_p10));  // open: dp
  nand nand_1 (n74160_1_p7, n74160_2_p10[0], n74160_2_p10[3], n74160_1_p10[0], n74160_1_p10[2]);
  Hex_Digit_Display hex_digit_display_9 (.value(n74160_3_p10));  // open: dp
  // _74160 74160_3: pin names not known; wires that end beside it: 1'b0, 1'b0, 1'b0, 1'b0, n74160_3_p5, n74160_3_p5, n74160_3_p7, 1'b1, n74160_1_p7, n74160_3_p10[0], n74160_3_p10[1], n74160_3_p10[2], n74160_3_p10[3]
  // _74160 74160_4: pin names not known; wires that end beside it: 1'b0, 1'b0, 1'b0, 1'b0, 1'b1, 1'b1, n74160_3_p7, 1'b1, n74160_1_p7, n74160_4_p10[0], n74160_4_p10[1], n74160_4_p10[2], n74160_4_p10[3], n74160_3_p5
  Hex_Digit_Display hex_digit_display_10 (.value(n74160_4_p10));  // open: dp
  nand nand_2 (n74160_3_p7, n74160_4_p10[0], n74160_4_p10[3], n74160_3_p10[0], n74160_3_p10[2]);
  Hex_Digit_Display hex_digit_display_11 (.value(n74160_5_p10));  // open: dp
  // _74160 74160_5: pin names not known; wires that end beside it: 1'b0, 1'b0, 1'b0, 1'b0, n74160_5_p5, n74160_5_p5, n74160_5_p7, 1'b1, n74160_3_p7, n74160_5_p10[0], n74160_5_p10[1], n74160_5_p10[2], n74160_5_p10[3]
  Hex_Digit_Display hex_digit_display_12 (.value(n74160_6_p10));  // open: dp
  // _74160 74160_6: pin names not known; wires that end beside it: 1'b0, 1'b0, 1'b0, 1'b0, 1'b1, 1'b1, n74160_5_p7, 1'b1, n74160_3_p7, n74160_6_p10[0], n74160_6_p10[1], n74160_6_p10[2], n74160_6_p10[3], n74160_5_p5
  nand nand_3 (n74160_5_p7, n74160_6_p10[0], n74160_5_p10[0]);
endmodule
